# Fritzing sketch fritzing scheme (saved by Fritzing 1.0.0rc)
breadboards: 1

parts:
  A1 = Particle - Photon2
  Part1 = Adafruit USB DC Solar LiPo Charger [part_number="Adafruit #390"]
  Part2 = Solar Panel [package="Renogy 50 Watts 12 Volt Monocrystalline Bendable Solar Panel"]
  U1 = LIPO-1000mAh [package=lipo-1000]
  U2 = WS2812 RGB LED strip
  J1 = Basic Servo
  Part3 = 16-Channel 12-bit PWM Servo Driver - I2C [part_number=815]
  J2 = Basic Servo
  J3 = Basic Servo
  J4 = Basic Servo
  J5 = Basic Servo
  JACK1 = 2.1mm Barrel Jack with Terminal Block
  U3 = WS2812 RGB LED strip
  U4 = WS2812 RGB LED strip
  U5 = WS2812 RGB LED strip
  U6 = WS2812 RGB LED strip
  U7 = WS2812 RGB LED strip
  U8 = WS2812 RGB LED strip
  U9 = WS2812 RGB LED strip

nets:
  N1: A1.Pin_2, A1.Pin_31, Part3.VCC
  GND: A1.Pin_4, A1.Pin_30, Part1.GND, U1.-, U2.GND, J1.gnd, Part3.GND, J2.gnd, J3.gnd, J4.gnd, J5.gnd, U3.GND, U4.GND, U5.GND, U6.GND, U7.GND, U8.GND, U9.GND
  N2: A1.Pin_17, Part3.SDA
  N3: A1.Pin_18, Part3.SCL
  N4: A1.Pin_19, U2.DIN, U2.DOUT, U3.DIN, U4.DIN, U5.DIN, U6.DIN, U7.DIN, U8.DIN, U9.DIN
  VCC: A1.Pin_26, Part1.LOAD, U2.VCC, J1.vcc, J3.vcc, J4.vcc, J5.vcc, U3.VCC, U4.VCC, U5.VCC, U6.VCC, U7.VCC, U8.VCC, U9.VCC
  N5: Part1.BATT, U1.+
  N6: Part2.Connector_1, JACK1.POS
  N7: Part2.Connector_2, JACK1.NEG
  N8: J1.pulse, Part3.PWM0
  N9: Part3.PWM4, J5.pulse
  N10: Part3.PWM3, J4.pulse
  N11: Part3.PWM2, J3.pulse
  N12: Part3.PWM1, J2.pulse

custom parts:
  Particle - Photon2: The Photon 2 is a microcontroller and Wi-Fi networking developed by particle. Features: 802.11a/b/g/n Wi-Fi, 2.4 GHz and 5 GHz Integrated PCB antenna Integrated U.FL connector for external antenna Integrated RF switch BLE 5 using same antenna as Wi-Fi Realtek RTL8721DM MCU ARM Cortex M33 CPU, 200 MHz 2048 KB (2 MB) user application maximum size 3072 KB (3 MB) of RAM available to user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
  Adafruit USB DC Solar LiPo Charger: Make your projects to go green this summer with our specialized USB/Solar Lithium Ion Polymer Battery charger! This charger is a very unique design, perfect for outdoor projects, or DIY iPod chargers. We've spent over a year testing and tinkering with this charger to come up with a plug and play solution to charging batteries with the sun and we're really pleased with what we ended up with.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
  Solar Panel: Renogy 50 Watts 12 Volt Solar Panel
  WS2812 RGB LED strip: WS2812 strip
  16-Channel 12-bit PWM Servo Driver - I2C: You want to make a cool robot, maybe a hexapod walker, or maybe just a piece of art with a lot of moving parts. Or maybe you want to drive a lot of LEDs with precise PWM output. Using only two pins, control 16 free-running PWM outputs! You can even chain up 62 breakouts to control up to 992 PWM outputs.
